# Fritzing sketch schematic_bb (saved by Fritzing 0.9.3b)
breadboards: 1

parts:
  Raspberry_Pi_1 = Raspberry Pi 3 [part_number=RPI-3-V1.2]
  LED1 = RGB LED (com. cathode, rgb) [package="5 mm [THT]"]
  S1 = Pushbutton [package="[THT]"]

nets:
  N1: Raspberry_Pi_1.3v3, LED1.common_cathode
  N2: Raspberry_Pi_1.GPIO2, LED1.red_anode
  N3: Raspberry_Pi_1.GPIO3, S1.Pin_3, S1.Pin_4
  N4: Raspberry_Pi_1.GPIO4, LED1.blue_anode
  N5: Raspberry_Pi_1.GND, S1.Pin_1, S1.Pin_2
  N6: Raspberry_Pi_1.GPIO14, LED1.green_anode

notes:
  TimeLapse project: https://goo.gl/9r6bwz
  Schematic for RGB Anode
